# Fritzing sketch Bai1,2,3Sketch (saved by Fritzing 0.9.5d)
circuit board: 8.46667cm x 5.64444cm
breadboards: 1

parts:
  S1 = Pushbutton [package="[THT]"]
  U1 = ESP32-38PinWide [part_number=ESP32-38PinWide]
  LED1 = smd LED [color="Red (633nm)" package="1206 [SMD]"]
  U2 = POT [package=alps_pot]

nets:
  N1: S1.Pin_1, S1.Pin_2, U1.GND, LED1.anode, U2.S
  N2: S1.Pin_3, S1.Pin_4, U1.GPIO25
  N3: U1.3.3, U2.A
  N4: U1.GPIO35, U2.E
  N5: U1.GPIO27, LED1.cathode

custom parts:
  ESP32-38PinWide: Generic 38-Pin ESP32 with wide format (only access to one side of pins on a breadboard) based on Stephen Lilley's HiLetgo ESP-WROOM-32 ESP32 ESP-32S Development Board.

// code stored in the sketch: esp32code123.ino

#define BUTTON_PIN 25
#define LED 27
#define ADC 35
#define N 32

int buffer[N] = {0};
int start = 0;
int samples = 0;

volatile bool buttonPressed = false;
volatile uint32_t drueke = 0, vorher = 0;

// Interrupt with debouncing
void IRAM_ATTR debounceShield() {
    uint32_t jetzt = millis();

    if (jetzt - vorher > 100) {
        drueke++;
        vorher = jetzt;
        buttonPressed = true;
    }
}

// Moving average filter
int filter(int m) {
    buffer[start] = m;
    start = (start + 1) % N;

    if (samples < N) samples++;

    long total = 0;
    for (int i = 0; i < N; i++) {
        total += buffer[i];
    }

    return total / samples;
}

void setup() {
    Serial.begin(115200);

    pinMode(BUTTON_PIN, INPUT_PULLUP);
    ledcAttach(LED, 5000, 8);

    attachInterrupt(
        digitalPinToInterrupt(BUTTON_PIN),
        debounceShield,
        FALLING
    );
}

void loop() {
    static int blinkState = 0;
    static uint32_t blinkTime = 0;
    static uint32_t sampleTime = 0;
    static int processed = 0;

    uint32_t now = millis();

    // Detect button press
    if (buttonPressed) {
        buttonPressed = false;
        blinkState = 1;
        blinkTime = now;
    }

    // Nonblocking LED flash
    if (blinkState == 1 &&
        now - blinkTime >= 80) {
        blinkState = 2;
        blinkTime = now;
    }
    else if (blinkState == 2 &&
             now - blinkTime >= 80) {
        blinkState = 0;
    }

    // Sample ADC every 20 ms
    if (now - sampleTime >= 20) {
        sampleTime = now;

        int raw = analogRead(ADC);
        processed = filter(raw);

        Serial.print(">tho:");
        Serial.println(raw);

        Serial.print(">loc:");
        Serial.println(processed);
    }

    // Control LED brightness
    if (blinkState == 1) {
        ledcWrite(LED, 0);
    }
    else if (blinkState == 2) {
        ledcWrite(LED, 255);
    }
    else {
        ledcWrite(
            LED,
            map(processed, 0, 4095, 0, 255)
        );
    }
}
